# Fritzing sketch tempControl (saved by Fritzing 0.9.3b)
circuit board: 8.46667cm x 5.64444cm
breadboards: 1

parts:
  Bauteil1 = Arduino Nano (Rev3.0)
  Bauteil2 = Adafruit Thermocouple Amplifier MAX31855 [part_number="Adafruit #269"]

nets:
  GND: Bauteil1.GND, Bauteil2.GND
  N1: Bauteil1.D3, Bauteil2.CLK
  N2: Bauteil1.D4, Bauteil2.CS
  N3: Bauteil1.D5, Bauteil2.DO
  3V3: Bauteil1.3V3, Bauteil2.+3V3

custom parts:
  Adafruit Thermocouple Amplifier MAX31855: Thermocouples are very sensitive, requiring a good amplifier with a cold-compensation reference. The MAX31855K does everything for you, and can be easily interfaced with any microcontroller, even one without an analog input. This breakout board has the chip itself, a 3.3V regulator with 10uF bypass capacitors and level shifting circuitry, all assembled and tested. Comes with a 2 pin terminal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
